# Fritzing sketch pcb (saved by Fritzing 0.9.3b)
circuit board: 8.46667cm x 5.64444cm
breadboards: 1

parts:
  botRec = Pushbutton [package="[THT]"]
  C100µF = Electrolytic Capacitor [capacitance=100µF voltage=16V package="100 mil [THT, electrolytic]"]
  RFimRecol = Resistor [tolerance=±5% resistance=100 package=THT]
  RfimInje = Resistor [tolerance=±5% resistance=100 package=THT]
  Rbr100Ω = Resistor [tolerance=±5% resistance=100 package=THT]
  Nema14 = Stepper Motor - Bipolar
  A4988 = Pololu A4988 [package=SO16]
  botPa = Pushbutton [package="[THT]"]
  RLver = Resistor [tolerance=±5% resistance=100 package=THT]
  LV = LED - 5mm [color="Green (570nm)" package="5 mm [THT]"]
  R3lVerd = Resistor [tolerance=±5% resistance=100 package=THT]
  Rbp100Ω = Resistor [tolerance=±5% resistance=100 package=THT]
  FCrec = Toggle Switch [package=THT]
  FCinj = Toggle Switch [package=THT]
  Part1 = Arduino Uno (Rev3)
  botIn = Pushbutton [package="[THT]"]
  Rbi100Ω = Resistor [tolerance=±5% resistance=100 package=THT]
  Buzzer = Piezo Speaker
  LM317 = Voltage Regulator [part_number=LM package=to220-adj]
  Lvm = LED - 3mm [color="Red (633nm)" package="3 mm [THT]"]
  R68Ω = Resistor [tolerance=±5% resistance=68 package=THT]
  R220 = Resistor [tolerance=±5% resistance=220 package=THT]

nets:
  N1: botRec.Pin_1, botRec.Pin_2, Rbr100Ω.Pin_0, Part1.D10_PWM/SS
  VDD: botRec.Pin_3, botRec.Pin_4, A4988.VDD, botPa.Pin_3, botPa.Pin_4, FCrec.L2, FCinj.L2, Part1.3V3, botIn.Pin_3, botIn.Pin_4
  N2: C100µF.-, A4988.GND#14, LM317.ADJ, R68Ω.Pin_0
  N3: C100µF.+, A4988.VMOT, LM317.OUT
  N4: RFimRecol.Pin_0, FCrec.COM, Part1.D8
  N5: RFimRecol.Pin_1, RfimInje.Pin_1, Rbr100Ω.Pin_1, A4988.GND#8, LV.cathode, Rbp100Ω.Pin_1, Part1.GND, Rbi100Ω.Pin_1, Buzzer.pin1, Lvm.cathode
  N6: RfimInje.Pin_0, FCinj.COM, Part1.D9_PWM
  N7: Nema14.A, A4988.2A
  N8: Nema14.C, A4988.1A
  N9: Nema14.B, A4988.1B
  N10: Nema14.D, A4988.2B
  N11: A4988.ENABLE, Part1.D5_PWM
  N12: A4988.RESET, A4988.SLEEP
  N13: A4988.STEP, Part1.D4
  N14: A4988.DIR, Part1.D3_PWM
  N15: botPa.Pin_1, botPa.Pin_2, Rbp100Ω.Pin_0, Part1.D6_PWM
  N16: RLver.Pin_0, RLver.Pin_1, Part1.D7, Lvm.anode
  N17: LV.anode, R3lVerd.Pin_0, R3lVerd.Pin_1, Part1.D13/SCK
  N18: Part1.D11_PWM/MOSI, botIn.Pin_1, botIn.Pin_2, Rbi100Ω.Pin_0
  N19: Part1.D12/MISO, Buzzer.pin2
  N20: LM317.IN, R68Ω.Pin_1, R220.Pin_0

notes:
  Fonte 12V 1A
  capacitor eletrolitico 100uF
  Negativo plug
  5V
  miLEDA 1.10

// code stored in the sketch: Untitled3.ino

